# Fritzing sketch v1 (saved by Fritzing 0.9.3b)
circuit board: 7.2cm x 6cm
breadboards: 1

parts:
  Part1 = Arduino Nano (Rev3.0)
  J1 = Camdenboss CTB0158-2 [part_number=CTB0158-2 package=THT]
  J3 = female pin header, 6 pins [form="♀ (female)"]
  J4 = female pin header, 6 pins [form="♀ (female)"]
  J2 = female pin header, 6 pins [form="♀ (female)"]
  J8 = female pin header, 6 pins [form="♀ (female)"]
  J6 = female pin header, 6 pins [form="♀ (female)"]
  S3 = Pushbutton [package="[THT]"]
  S4 = Pushbutton [package="[THT]"]
  LED1 = LED - 5mm [color="Red (633nm)" package="5 mm [THT]"]
  R1 = Resistor [tolerance=±5% resistance=470 package="1206 [SMD]"]
  J12 = female pin header, 7 pins [form="♀ (female)"]
  J9 = female pin header, 4 pins [form="♀ (female)"]
  J14 = female pin header, 4 pins [form="♀ (female)"]
  J16 = female pin header, 4 pins [form="♀ (female)"]
  J17 = female pin header, 2 pins [form="♀ (female)"]
  J18 = female pin header, 1 pin [form="♀ (female)"]
  J19 = female pin header, 3 pins [form="♀ (female)"]

nets:
  N1: Part1.D1/TX, J9.pin1
  N2: Part1.D0/RX, J9.pin2
  N3: Part1.RESET, J18.pin1
  GND: Part1.GND, J1.pin1, J3.pin1, J3.pin2, J3.pin3, J3.pin4, J3.pin5, J3.pin6, J6.pin1, J6.pin2, J6.pin3, J6.pin4, J6.pin5, J6.pin6, S3.Pin_3, S3.Pin_4, S4.Pin_3, S4.Pin_4, LED1.cathode, J12.pin1, J9.pin3
  N4: Part1.D2, J12.pin2
  N5: Part1.D3, R1.Pin_0, J12.pin3
  N6: Part1.D4, S3.Pin_1, S3.Pin_2, J12.pin4
  N7: Part1.D5, J12.pin5
  N8: Part1.D6, J12.pin6
  N9: Part1.D7, S4.Pin_1, S4.Pin_2, J12.pin7
  N10: Part1.D8, J2.pin1
  N11: Part1.D9, J2.pin2
  N12: Part1.D10, J2.pin3
  N13: Part1.D11/MOSI, J2.pin4
  N14: Part1.D12/MISO, J2.pin5
  5V: Part1.VIN, J4.pin1, J4.pin2, J4.pin3, J4.pin4, J4.pin5, J4.pin6, J19.pin3
  N15: Part1.5V, J8.pin1, J8.pin2, J8.pin3, J8.pin4, J8.pin5, J8.pin6, J9.pin4
  N16: Part1.A7, J16.pin1
  N17: Part1.A6, J16.pin2
  N18: Part1.A5, J16.pin3
  N19: Part1.A4, J16.pin4
  N20: Part1.A3, J14.pin1
  N21: Part1.A2, J14.pin2
  N22: Part1.A1, J14.pin3
  N23: Part1.A0, J14.pin4
  N24: Part1.AREF, J17.pin1
  N25: Part1.3V3, J17.pin2
  N26: Part1.D13/SCK, J2.pin6
  N27: J1.pin2, J19.pin2
  N28: LED1.anode, R1.Pin_1
